# Fritzing sketch Chamarande (saved by Fritzing 0.9.3b)

parts:
  Power_plug1 = Power plug
  Composant1 = Adafruit Metro Mini [part_number="Adafruit #2590"]
  M1 = DC Motor
  M2 = DC Motor
  Composant2 = Motor Driver 1A Dual TB6612FNG

nets:
  GND: Power_plug1.GND, Composant1.GND, Composant2.GND
  VCC: Power_plug1.VCC, Composant1.VIN, Composant2.VCC, Composant2.VM
  N1: Composant1.IO12, Composant2.PWMB
  N2: Composant1.IO11, Composant2.BIN2
  N3: Composant1.IO10, Composant2.BIN1
  N4: Composant1.IO9, Composant2.STBY
  N5: Composant1.IO8, Composant2.AIN1
  N6: Composant1.IO7, Composant2.AIN2
  N7: Composant1.IO6, Composant2.PWMA
  N8: M1.pin_1, Composant2.B01
  N9: M1.pin_2, Composant2.B02
  N10: M2.pin_1, Composant2.A02
  N11: M2.pin_2, Composant2.A01

custom parts:
  Adafruit Metro Mini: We sure love the ATmega328 here at Adafruit, and we use them a lot for our own projects. The processor has plenty of GPIO, Analog inputs, hardware UART SPI and I2C, timers and PWM galore - just enough for most simple projects. When we need to go small, we use a Pro Trinket 3V or 5V, but if you want to have USB-to-Serial built in, we reach for an Adafruit METRO Mini. METRO Mini is the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
